# Fritzing sketch schematic_without_shield (saved by Fritzing 0.9.3b)
breadboards: 1

parts:
  MQ-9_Gas_Sensor_(CO_LPG_CH4) = MQ-9 breakout
  Grove_Dust_Sensor = Grove Dust Sensor
  MQ-7_Gas_Sensor_(CO) = MQ-131 breakout
  DHT-11_Sensor_(Temperature_Humidity) = Grove Temperature Sensor
  ESP8266_(Wi-Fi) = ESP8266 WiFi Module [part_number=ESP8266]
  Part1 = Arduino Nano (Rev3.0)

nets:
  VCC: MQ-9_Gas_Sensor_(CO_LPG_CH4).VCC, Grove_Dust_Sensor.VCC, MQ-7_Gas_Sensor_(CO).VCC, DHT-11_Sensor_(Temperature_Humidity).VCC, ESP8266_(Wi-Fi).VCC, Part1.5V
  GND: MQ-9_Gas_Sensor_(CO_LPG_CH4).GND, Grove_Dust_Sensor.GND, MQ-7_Gas_Sensor_(CO).GND, DHT-11_Sensor_(Temperature_Humidity).GND, ESP8266_(Wi-Fi).GND, Part1.GND
  N1: MQ-9_Gas_Sensor_(CO_LPG_CH4).AO, Part1.A2
  N2: Grove_Dust_Sensor.SIG, Part1.A1
  N3: Grove_Dust_Sensor.NC, Part1.A0
  N4: MQ-7_Gas_Sensor_(CO).AO, Part1.A3
  N5: DHT-11_Sensor_(Temperature_Humidity).SIG, Part1.D2
  N6: ESP8266_(Wi-Fi).RXD, Part1.D0/RX
  N7: ESP8266_(Wi-Fi).TXD, Part1.D1/TX

custom parts:
  MQ-9 breakout: SKU: 101284
  Grove Dust Sensor: PPD42 Grove Dust Sensor
  MQ-131 breakout: SKU: 101282
