# Fritzing sketch schematic_with_shield (saved by Fritzing 0.9.3b)

parts:
  Arduino_Uno = Arduino Uno (Rev3)
  Base_Shield = Base Shield V2
  MQ-9_Gas_Sensor_(CO_LPG_CH4) = MQ-9 breakout
  Grove_Dust_Sensor = Grove Dust Sensor
  MQ-7_Gas_Sensor_(CO) = MQ-131 breakout
  DHT-11_Sensor_(Temperature_Humidity) = Grove Temperature Sensor
  ESP8266_(Wi-Fi) = ESP8266 WiFi Module [part_number=ESP8266]

nets:
  N1: Arduino_Uno.A0, Base_Shield.A0
  N2: Arduino_Uno.A1, Base_Shield.A1
  N3: Arduino_Uno.A2, Base_Shield.A2
  N4: Arduino_Uno.A3, Base_Shield.A3
  N5: Arduino_Uno.A4/SDA, Base_Shield.A4
  N6: Arduino_Uno.A5/SCL, Base_Shield.A5
  N7: Arduino_Uno.D8, Base_Shield.D8
  N8: Arduino_Uno.D9_PWM, Base_Shield.D9
  N9: Arduino_Uno.D10_PWM/SS, Base_Shield.D10
  N10: Arduino_Uno.D11_PWM/MOSI, Base_Shield.D11
  N11: Arduino_Uno.D12/MISO, Base_Shield.D12
  N12: Arduino_Uno.D13/SCK, Base_Shield.D13
  GND: Arduino_Uno.GND, Base_Shield.GND, ESP8266_(Wi-Fi).GND
  N13: Arduino_Uno.AREF, Base_Shield.AREF
  N14: Arduino_Uno.D0/RX, Base_Shield.D0/RX, ESP8266_(Wi-Fi).RXD
  N15: Arduino_Uno.D1/TX, Base_Shield.D1/TX, ESP8266_(Wi-Fi).TXD
  N16: Arduino_Uno.D2, Base_Shield.D2
  N17: Arduino_Uno.D3_PWM, Base_Shield.D3
  N18: Arduino_Uno.D4, Base_Shield.D4
  N19: Arduino_Uno.D5_PWM, Base_Shield.D5
  N20: Arduino_Uno.D6_PWM, Base_Shield.D6_PWM
  N21: Arduino_Uno.D7, Base_Shield.D7
  N22: Arduino_Uno.ioref, Base_Shield.ioref
  N23: Arduino_Uno.RESET, Base_Shield.RESET
  3V3: Arduino_Uno.3V3, Base_Shield.3V3, ESP8266_(Wi-Fi).VCC
  5V: Arduino_Uno.5V, Base_Shield.5V
  VIN: Arduino_Uno.VIN, Base_Shield.VIN
  N24: Arduino_Uno.N/C, Base_Shield.N/C
  N25: Base_Shield.pin_96, DHT-11_Sensor_(Temperature_Humidity).GND
  N26: Base_Shield.pin_97, DHT-11_Sensor_(Temperature_Humidity).VCC
  N27: Base_Shield.pin_99, DHT-11_Sensor_(Temperature_Humidity).SIG
  N28: Base_Shield.pin_136, Grove_Dust_Sensor.GND
  N29: Base_Shield.pin_137, Grove_Dust_Sensor.VCC
  N30: Base_Shield.pin_139, Grove_Dust_Sensor.SIG
  N31: Base_Shield.pin_148, MQ-9_Gas_Sensor_(CO_LPG_CH4).AO
  N32: Base_Shield.pin_150, MQ-9_Gas_Sensor_(CO_LPG_CH4).GND
  N33: Base_Shield.pin_151, MQ-9_Gas_Sensor_(CO_LPG_CH4).VCC
  N34: Base_Shield.pin_152, MQ-7_Gas_Sensor_(CO).AO
  N35: Base_Shield.pin_154, MQ-7_Gas_Sensor_(CO).GND
  N36: Base_Shield.pin_155, MQ-7_Gas_Sensor_(CO).VCC

custom parts:
  MQ-9 breakout: SKU: 101284
  Grove Dust Sensor: PPD42 Grove Dust Sensor
  MQ-131 breakout: SKU: 101282
