# Fritzing sketch schematic_without_shield (saved by Fritzing 0.9.3b)
breadboards: 1

parts:
  Arduino_Uno = Arduino Uno (Rev3)
  MQ-9_Gas_Sensor_(CO_LPG_CH4) = MQ-9 breakout
  Grove_Dust_Sensor = Grove Dust Sensor
  MQ-7_Gas_Sensor_(CO) = MQ-131 breakout
  DHT-11_Sensor_(Temperature_Humidity) = Grove Temperature Sensor
  ESP8266_(Wi-Fi) = ESP8266 WiFi Module [part_number=ESP8266]

nets:
  N1: Arduino_Uno.A0, Grove_Dust_Sensor.NC
  N2: Arduino_Uno.A1, Grove_Dust_Sensor.SIG
  N3: Arduino_Uno.A2, MQ-9_Gas_Sensor_(CO_LPG_CH4).AO
  N4: Arduino_Uno.A3, MQ-7_Gas_Sensor_(CO).AO
  N5: Arduino_Uno.D0/RX, ESP8266_(Wi-Fi).RXD
  N6: Arduino_Uno.D1/TX, ESP8266_(Wi-Fi).TXD
  N7: Arduino_Uno.D2, DHT-11_Sensor_(Temperature_Humidity).SIG
  VCC: Arduino_Uno.5V, MQ-9_Gas_Sensor_(CO_LPG_CH4).VCC, Grove_Dust_Sensor.VCC, MQ-7_Gas_Sensor_(CO).VCC, DHT-11_Sensor_(Temperature_Humidity).VCC, ESP8266_(Wi-Fi).VCC
  GND: Arduino_Uno.GND, MQ-9_Gas_Sensor_(CO_LPG_CH4).GND, Grove_Dust_Sensor.GND, MQ-7_Gas_Sensor_(CO).GND, DHT-11_Sensor_(Temperature_Humidity).GND, ESP8266_(Wi-Fi).GND

custom parts:
  MQ-9 breakout: SKU: 101284
  Grove Dust Sensor: PPD42 Grove Dust Sensor
  MQ-131 breakout: SKU: 101282
